// Logisim project lab3-strasburg.circ as structural Verilog: 1 circuit, main circuit main
module main (
  input  in_1,
  input  in_2,
  input  in_3,
  input  in_4,
  input  in_5,
  input  A0,
  input  in_7,
  input  in_8,
  input  A1,
  input  in_10,
  input  in_11,
  input  in_12,
  input  A2,
  input  [3:0] in_14,
  input  in_15,
  input  A3,
  input  in_17,
  input  A4,
  input  A0_2,
  input  A5,
  input  B0,
  input  in_22,
  input  A1_2,
  input  A6,
  input  in_25,
  input  B1,
  input  A7,
  input  A2_2,
  input  B2,
  input  Reset,
  input  A3_2,
  input  B3,
  output B0_2,
  output B1_2,
  output out_35,
  output B2_2,
  output B3_2,
  output B4,
  output B5,
  output B6,
  output decoder,
  output B7,
  output out_43,
  output out_44,
  output out_45,
  output out_46
);

  wire _00_2_out, _01_2_out, _10_2_out, _11_2_out, clock_1_out, multiplexer_1_out, xor_1_out, xor_2_out,
       xor_3_out, xor_4_out;

  Clock clock_1 (.out(clock_1_out));
  D_Flip_Flop d_ff_1 (.clk(clock_1_out), .D(A0), .Q(B0_2), .reset(Reset));  // open: Qn, preset, en
  D_Flip_Flop d_ff_2 (.clk(clock_1_out), .D(A1), .Q(B1_2), .reset(Reset));  // open: Qn, preset, en
  D_Flip_Flop d_ff_3 (.clk(clock_1_out), .D(A2), .Q(B2_2), .reset(Reset));  // open: Qn, preset, en
  D_Flip_Flop d_ff_4 (.clk(clock_1_out), .D(A3), .Q(B3_2), .reset(Reset));  // open: Qn, preset, en
  D_Flip_Flop d_ff_5 (.clk(clock_1_out), .D(A4), .Q(B4), .reset(Reset));  // open: Qn, preset, en
  D_Flip_Flop d_ff_6 (.clk(clock_1_out), .D(A5), .Q(B5), .reset(Reset));  // open: Qn, preset, en
  D_Flip_Flop d_ff_7 (.clk(clock_1_out), .D(A6), .Q(B6), .reset(Reset));  // open: Qn, preset, en
  D_Flip_Flop d_ff_8 (.clk(clock_1_out), .D(A7), .Q(B7), .reset(Reset));  // open: Qn, preset, en
  // Probe on {B7, B6, B5, B4, B3_2, B2_2, B1_2, B0_2}
  Multiplexer #(.select(4)) multiplexer_1 (
    .in2(in_3), .in3(in_4), .in5(in_7), .in7(in_8), .in13(in_11), .out(multiplexer_1_out), .sel(in_14),
    .en(in_12));  // open: in0, in1, in4, in6, in8, in9, in10, in11, in12, in14, in15
  LED led_1 (.in(multiplexer_1_out));
  xor xor_1 (xor_1_out, A0_2, B0);
  xor xor_2 (xor_2_out, A1_2, B1);
  xor xor_3 (xor_3_out, A2_2, B2);
  xor xor_4 (xor_4_out, A3_2, B3);
  nor nor_1 (out_43, xor_1_out, xor_2_out, xor_3_out, xor_4_out);
  and _00 (decoder, ~in_22, ~in_25);  // AND_Gate
  and _01 (out_44, ~in_22, in_25);  // AND_Gate
  and _10 (out_45, in_22, ~in_25);  // AND_Gate
  and _11 (out_46, in_22, in_25);
  and _00_2 (_00_2_out, ~in_2, ~in_5, in_1);  // AND_Gate
  and _01_2 (_01_2_out, ~in_2, in_10, in_1);  // AND_Gate
  and _10_2 (_10_2_out, in_2, in_15, ~in_1);  // AND_Gate
  and _11_2 (_11_2_out, in_2, in_17, in_1);
  or or_1 (out_35, _00_2_out, _01_2_out, _10_2_out, _11_2_out);

  // Notes on the sheet:
  //   Set Clock
  //   8 Bit Register
  //   4 bit compare operator
  //   Set number on the Pin LED lights up if number is prime
  //   multiplexer
endmodule
