// Logisim project multiplexer.circ as structural Verilog: 1 circuit, main circuit main
module main (
  input  in_1,
  input  in_2,
  input  in_3,
  input  in_4,
  input  in_5,
  input  in_6,
  input  in_7,
  input  in_8,
  input  [2:0] in_9
);

  wire multiplexer_1_out, multiplexer_2_out, undriven, undriven_2;

  Multiplexer multiplexer_1 (.in0(in_2), .in1(in_1), .out(multiplexer_1_out), .sel(in_4), .en(in_3));
  LED led_1 (.in(multiplexer_1_out));
  LED led_2 (.in(multiplexer_2_out));
  Multiplexer #(.select(3)) multiplexer_2 (
    .in0(in_6), .in1(in_5), .in3(undriven), .in5(undriven_2), .in7(in_7), .out(multiplexer_2_out),
    .sel(in_9), .en(in_8));  // open: in2, in4, in6
endmodule
