// Logisim project register-inc.circ as structural Verilog: 1 circuit, main circuit main
module main (
  input  A0,
  input  A0_2,
  input  A0_3,
  input  A0_4,
  input  A0_5,
  output B0,
  output B0_2,
  output B0_3,
  output B0_4
);

  wire undriven;

  D_Flip_Flop d_ff_1 (.clk(undriven), .D(A0), .Q(B0), .reset(A0_5));  // open: Qn, preset, en
  D_Flip_Flop d_ff_2 (.clk(undriven), .D(A0_2), .Q(B0_2), .reset(A0_5));  // open: Qn, preset, en
  D_Flip_Flop d_ff_3 (.clk(undriven), .D(A0_3), .Q(B0_3), .reset(A0_5));  // open: Qn, preset, en
  D_Flip_Flop d_ff_4 (.clk(undriven), .D(A0_4), .Q(B0_4), .reset(A0_5));  // open: Qn, preset, en
  Clock clock_1 ();  // open: out
  // Probe on {B0_2, B0}
endmodule
